# Fritzing sketch Sensor_node (saved by Fritzing 0.9.6b)
circuit board: 8.46667cm x 5.64444cm
breadboards: 1

parts:
  VCC1 = 4 x AAA Battery Mount
  S1 = Toggle Switch [package=THT]
  Part1 = Arduino Nano (Rev3.0) (ICSP)
  DHT1 = DHT22 Humidity and Temperature Sensor
  Capacitive_Soil_Moisture_Sensor1 = DFRobot Capacitive Soil Moisture Sensor V1.0 [part_number=SEN0193]
  U1 = XBee
  R1 = Resistor [tolerance=±5% resistance=220 package="2010 [SMD]"]

nets:
  N1: VCC1.+, S1.L1
  N2: S1.L2, Part1.VIN
  N3: Part1.D1/TX, U1.pin3
  N4: Part1.D0/RX, U1.pin2
  GND: Part1.GND, DHT1.GND, Capacitive_Soil_Moisture_Sensor1.GND, U1.GND
  N5: Part1.D2, DHT1.DATA, R1.Pin_1
  N6: Part1.A0, Capacitive_Soil_Moisture_Sensor1.A
  VCC: DHT1.VDD, Capacitive_Soil_Moisture_Sensor1.VCC, U1.VCC, R1.Pin_0

custom parts:
  DFRobot Capacitive Soil Moisture Sensor V1.0: DFRobot Capacitive Soil Moisture Sensor V1.0 This product measures soil moisture levels by capacitive sensing, rather than resistive sensing like other types of moisture sensor. It is made of a corrosion resistant material giving it a long service life. Insert it into soil and impress your friends with the real-time soil moisture data! The product includes an on-board voltage regulator which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
  XBee: XBee embedded RF module.
